# Fritzing sketch Diodes (saved by Fritzing 0.9.10b)
breadboards: 1

parts:
  D1 = Rectifier Diode [part_number=1N4001 package="300 mil [THT]"]  # not connected
  M2 = Arduino NANO RP2040 CONNECT with headers
  LED3 = smd LED [color="Red (633nm)" package="1206 [SMD]"]

nets:
  N1: M2.GND-4, M2.GND-29, LED3.cathode

custom parts:
  Arduino NANO RP2040 CONNECT with headers: Meet the only connected RP2040 board. It fits the Arduino Nano form factor, making it a small board with BIG features. The brain of the board is the Raspberry Pi RP2040 silicon; a dual-core Arm Cortex M0+ running at 133MHz. It has 264KB of SRAM, and the 16MB of flash memory is off-chip to give you extra storage. But what’s really exciting is the on-board connectivity options. The hugely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
