# Fritzing sketch AnalogReadPoti (saved by Fritzing 0.9.10b)

parts:
  M1 = Arduino Nano 33 IOT-tht
  U3 = POT [knob_status=50% power=0.5W package=pot_mammoth]

nets:
  N1: M1.pin_2, U3.E
  N2: M1.pin_4, U3.A
  N3: M1.pin_14, U3.S

custom parts:
  Arduino Nano 33 IOT-tht: The Arduino Nano 33 IoT is the easiest and cheapest point of entry to enhance existing devices (and creating new ones) to be part of the IoT and designing pico-network applications. Whether you are looking at building a sensor network connected to your office or home router, or if you want to create a BLE device sending data to a cellphone, the Nano 33 IoT is your one-stop-solution for many of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
