# Fritzing sketch AnalogReadLightDiode (saved by Fritzing 0.9.10b)
breadboards: 1

parts:
  M1 = Arduino Nano 33 IOT-tht
  P1 = S1133 Si Photodiode [package="8mm Ceramic [THT]"]
  R1 = Resistor [tolerance=±5% resistance=1M package="2512 [SMD]"]

nets:
  N1: M1.pin_2, M1.pin_4, R1.Pin_1
  N2: M1.pin_13, M1.pin_18
  N3: M1.pin_14, M1.pin_19, P1.cathode
  N4: P1.anode, R1.Pin_0

custom parts:
  Arduino Nano 33 IOT-tht: The Arduino Nano 33 IoT is the easiest and cheapest point of entry to enhance existing devices (and creating new ones) to be part of the IoT and designing pico-network applications. Whether you are looking at building a sensor network connected to your office or home router, or if you want to create a BLE device sending data to a cellphone, the Nano 33 IoT is your one-stop-solution for many of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
